# Fritzing sketch Circuit Diagram (saved by Fritzing 0.9.10b)
breadboards: 1

parts:
  Part1 = Adafruit ADS1115 16Bit I2C ADC [part_number="Adafruit #1085"]
  U1 = ESP32-38PinWide [part_number=ESP32-38PinWide]
  J1 = Screw terminal - 2 pins [package=THT]
  J2 = Screw terminal - 2 pins [package=THT]
  LED1 = LEDs [package=led10mm]  # not connected
  LED2 = LEDs [package=led10mm]  # not connected

nets:
  N1: Part1.AIN1, J2.pin2
  N2: Part1.AIN0, J1.pin1
  N3: Part1.SDA, U1.GPIO21
  N4: Part1.SCL, U1.GPIO22
  GND: Part1.GND, U1.GND, J1.pin2, J2.pin1
  N5: Part1.VDD, U1.3.3

custom parts:
  Adafruit ADS1115 16Bit I2C ADC: For microcontrollers without an analog-to-digital converter or when you want a higher-precision ADC, the ADS1115 provides 16-bit precision at 860 samples/second over I2C. The chip can be configured as 4 single-ended input channels, or two differential channels. As a nice bonus, it even includes a programmable gain amplifier, up to x16, to help boost up smaller single/differential signals to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
  ESP32-38PinWide: Generic 38-Pin ESP32 with wide format (only access to one side of pins on a breadboard) based on Stephen Lilley's HiLetgo ESP-WROOM-32 ESP32 ESP-32S Development Board.
